// Logisim project DustcatV.circ as structural Verilog: 9 circuits, main circuit DustcatV
module DustcatV (
);

  wire MCLK;

  Clock clock_1 (.out(MCLK));
  ExecutionUnit executionunit_1 ();  // open: CDBIn, Instruction, Clk, Clear, CDB1, CDB2, IntFull, VAddress, Data, Load, Store, LoadStoreFull
endmodule

module ExecutionUnit (
  input  [31:0] CDBIn,
  input  [31:0] Instruction,
  input  Clk,
  input  Clear,
  output [31:0] CDB1,
  output [31:0] CDB2,
  output IntFull,
  output [23:0] VAddress,
  output [15:0] Data,
  output Load,
  output Store,
  output LoadStoreFull
);

  wire and_1_out, and_2_out, commit1, commit2, comparator_1_eq, comparator_2_eq, comparator_3_eq,
       comparator_4_eq, demultiplexer_1_out0, demultiplexer_1_out1, demultiplexer_1_out2,
       demultiplexer_1_out3, demultiplexer_1_out4, demultiplexer_1_out5, demultiplexer_1_out6,
       demultiplexer_1_out7, demultiplexer_3_out0, demultiplexer_3_out1, demultiplexer_3_out2,
       demultiplexer_3_out3, demultiplexer_3_out4, demultiplexer_3_out5, demultiplexer_3_out6,
       demultiplexer_3_out7, demultiplexer_4_out0, demultiplexer_4_out1, demultiplexer_4_out2,
       demultiplexer_4_out3, demultiplexer_4_out4, demultiplexer_4_out5, demultiplexer_4_out6,
       demultiplexer_4_out7, demultiplexer_5_out0, demultiplexer_5_out1, demultiplexer_5_out2,
       demultiplexer_6_out8, demultiplexer_6_out9, demultiplexer_6_out10, loadstoretranslator_1_done,
       not_1_out, not_2_out, or_1_out, or_2_out, or_3_out, or_4_out, or_5_out, or_6_out, or_7_out, or_8_out,
       or_9_out, priority_encoder_1_gs, priority_encoder_3_gs, priority_encoder_5_gs, register_2_q,
       register_4_q, register_6_q, reservationstation_1_empty, reservationstation_1_ready,
       reservationstation_2_empty, reservationstation_2_ready, reservationstation_3_empty,
       reservationstation_3_ready, reservationstation_4_empty, reservationstation_4_ready,
       reservationstation_5_empty, reservationstation_5_ready, reservationstation_6_empty,
       reservationstation_6_ready, reservationstation_7_empty, reservationstation_7_ready,
       reservationstation_8_empty, reservationstation_8_ready, reservationstation_9_empty,
       reservationstation_9_ready, reservationstation_10_empty, reservationstation_10_ready,
       reservationstation_11_empty, reservationstation_11_ready;
  wire [1:0] priority_encoder_1_out, priority_encoder_3_out, priority_encoder_5_out, register_1_q,
       register_3_q, register_5_q;
  wire [2:0] priority_encoder_4_p5, pull_resistor_6_node;
  wire [3:0] multiplexer_5_out, pull_resistor_1_node, pull_resistor_4_node, reservationstation_1_stationid,
       reservationstation_2_stationid, reservationstation_3_stationid, reservationstation_4_stationid,
       reservationstation_5_stationid, reservationstation_6_stationid, reservationstation_7_stationid,
       reservationstation_8_stationid, reservationstation_9_stationid, reservationstation_10_stationid,
       reservationstation_11_stationid;
  wire [7:0] multiplexer_4_out, multiplexer_8_out, multiplexer_13_out, reservationstation_1_instop,
       reservationstation_2_instop, reservationstation_3_instop, reservationstation_4_instop,
       reservationstation_5_instop, reservationstation_6_instop, reservationstation_7_instop,
       reservationstation_8_instop, reservationstation_9_instop, reservationstation_10_instop,
       reservationstation_11_instop;
  wire [15:0] functionalunit_1_result, functionalunit_2_result, multiplexer_1_out, multiplexer_2_out,
       multiplexer_3_out, multiplexer_6_out, multiplexer_7_out, multiplexer_10_out, multiplexer_11_out,
       pull_resistor_8_node, pull_resistor_11_node, reservationstation_1_immoraddr,
       reservationstation_1_operand1, reservationstation_1_operand2, reservationstation_2_immoraddr,
       reservationstation_2_operand1, reservationstation_2_operand2, reservationstation_3_immoraddr,
       reservationstation_3_operand1, reservationstation_3_operand2, reservationstation_4_immoraddr,
       reservationstation_4_operand1, reservationstation_4_operand2, reservationstation_5_operand1,
       reservationstation_5_operand2, reservationstation_6_immoraddr, reservationstation_6_operand1,
       reservationstation_6_operand2, reservationstation_7_immoraddr, reservationstation_7_operand1,
       reservationstation_7_operand2, reservationstation_8_immoraddr, reservationstation_8_operand1,
       reservationstation_8_operand2, reservationstation_9_immoraddr, reservationstation_9_operand1,
       reservationstation_9_operand2, reservationstation_10_immoraddr, reservationstation_10_operand1,
       reservationstation_10_operand2, reservationstation_11_immoraddr, reservationstation_11_operand1,
       reservationstation_11_operand2, undriven;
  wire [31:0] demultiplexer_2_out0, demultiplexer_2_out1;

  Demultiplexer #(.select(4), .enable("false")) demultiplexer_1 (
    .out0(demultiplexer_1_out0), .out1(demultiplexer_1_out1), .out2(demultiplexer_1_out2),
    .out3(demultiplexer_1_out3), .out4(demultiplexer_1_out4), .out5(demultiplexer_1_out5),
    .out6(demultiplexer_1_out6), .out7(demultiplexer_1_out7), .in(commit2), .sel(pull_resistor_1_node));  // open: out8, out9, out10, out11, out12, out13, out14, out15
  Pull_Resistor pull_resistor_1 (.node(pull_resistor_1_node));
  Comparator comparator_1 (.a(8'h21), .b(Instruction[31:24]), .eq(comparator_1_eq));  // open: gt, lt
  Comparator comparator_2 (.a(Instruction[31:24]), .b(8'h20), .eq(comparator_2_eq));  // open: gt, lt
  Pull_Resistor pull_resistor_2 (.node(Clk));
  Pull_Resistor pull_resistor_3 (.node(Clear));
  Pull_Resistor pull_resistor_4 (.node(pull_resistor_4_node));
  Demultiplexer #(.width(32), .enable("false")) demultiplexer_2 (
    .out0(demultiplexer_2_out0), .out1(demultiplexer_2_out1), .in(Instruction), .sel(or_1_out));
  or or_1 (or_1_out, comparator_1_eq, comparator_2_eq);
  or or_2 (or_2_out, Clear, demultiplexer_1_out0, demultiplexer_3_out0);
  or or_3 (or_3_out, Clear, demultiplexer_1_out1, demultiplexer_3_out1);
  or or_4 (or_4_out, Clear, demultiplexer_1_out2, demultiplexer_3_out2);
  or or_5 (or_5_out, Clear, demultiplexer_1_out3, demultiplexer_3_out3);
  or or_6 (or_6_out, Clear, demultiplexer_1_out4, demultiplexer_3_out4);
  or or_7 (or_7_out, Clear, demultiplexer_1_out5, demultiplexer_3_out5);
  or or_8 (or_8_out, Clear, demultiplexer_1_out6, demultiplexer_3_out6);
  or or_9 (or_9_out, Clear, demultiplexer_1_out7, demultiplexer_3_out7);
  Demultiplexer #(.select(4), .enable("false")) demultiplexer_3 (
    .out0(demultiplexer_3_out0), .out1(demultiplexer_3_out1), .out2(demultiplexer_3_out2),
    .out3(demultiplexer_3_out3), .out4(demultiplexer_3_out4), .out5(demultiplexer_3_out5),
    .out6(demultiplexer_3_out6), .out7(demultiplexer_3_out7), .in(commit1), .sel(pull_resistor_4_node));  // open: out8, out9, out10, out11, out12, out13, out14, out15
  not not_1 (not_1_out, comparator_3_eq);
  Comparator #(.width(32)) comparator_3 (
    .a({32{1'b0}}), .b(demultiplexer_2_out0), .eq(comparator_3_eq));  // open: gt, lt
  Comparator #(.width(32)) comparator_4 (
    .a({32{1'b0}}), .b(demultiplexer_2_out1), .eq(comparator_4_eq));  // open: gt, lt
  Pull_Resistor pull_resistor_5 (.node(commit1));
  Demultiplexer #(.select(3), .enable("false")) demultiplexer_4 (
    .out0(demultiplexer_4_out0), .out1(demultiplexer_4_out1), .out2(demultiplexer_4_out2),
    .out3(demultiplexer_4_out3), .out4(demultiplexer_4_out4), .out5(demultiplexer_4_out5),
    .out6(demultiplexer_4_out6), .out7(demultiplexer_4_out7), .in(not_1_out), .sel(pull_resistor_6_node));
  not not_2 (not_2_out, comparator_4_eq);
  Demultiplexer #(.select(3), .enable("false")) demultiplexer_5 (
    .out0(demultiplexer_5_out0), .out1(demultiplexer_5_out1), .out2(demultiplexer_5_out2), .in(not_2_out),
    .sel(priority_encoder_4_p5));  // open: out3, out4, out5, out6, out7
  Demultiplexer #(.select(4), .enable("false")) demultiplexer_6 (
    .out8(demultiplexer_6_out8), .out9(demultiplexer_6_out9), .out10(demultiplexer_6_out10),
    .in(loadstoretranslator_1_done), .sel(multiplexer_5_out));  // open: out0, out1, out2, out3, out4, out5, out6, out7, out11, out12, out13, out14, out15
  ReservationStation reservationstation_1 (
    .IdIn(4'b0000), .Instruction(demultiplexer_2_out0), .CDBIn(CDBIn), .clk(Clk),
    .StationSelect(demultiplexer_4_out0), .Clear(or_2_out), .Operand1(reservationstation_1_operand1),
    .Operand2(reservationstation_1_operand2), .InstOp(reservationstation_1_instop),
    .ImmOrAddr(reservationstation_1_immoraddr), .StationId(reservationstation_1_stationid),
    .Ready(reservationstation_1_ready), .Empty(reservationstation_1_empty));
  and and_1 (and_1_out, commit1, Clk);
  ReservationStation reservationstation_2 (
    .IdIn(reservationstation_1_stationid), .Instruction(demultiplexer_2_out0), .CDBIn(CDBIn), .clk(Clk),
    .StationSelect(demultiplexer_4_out1), .Clear(or_3_out), .Operand1(reservationstation_2_operand1),
    .Operand2(reservationstation_2_operand2), .InstOp(reservationstation_2_instop),
    .ImmOrAddr(reservationstation_2_immoraddr), .StationId(reservationstation_2_stationid),
    .Ready(reservationstation_2_ready), .Empty(reservationstation_2_empty));
  ReservationStation reservationstation_3 (
    .IdIn(reservationstation_2_stationid), .Instruction(demultiplexer_2_out0), .CDBIn(CDBIn), .clk(Clk),
    .StationSelect(demultiplexer_4_out2), .Clear(or_4_out), .Operand1(reservationstation_3_operand1),
    .Operand2(reservationstation_3_operand2), .InstOp(reservationstation_3_instop),
    .ImmOrAddr(reservationstation_3_immoraddr), .StationId(reservationstation_3_stationid),
    .Ready(reservationstation_3_ready), .Empty(reservationstation_3_empty));
  ReservationStation reservationstation_4 (
    .IdIn(reservationstation_3_stationid), .Instruction(demultiplexer_2_out0), .CDBIn(CDBIn), .clk(Clk),
    .StationSelect(demultiplexer_4_out3), .Clear(or_5_out), .Operand1(reservationstation_4_operand1),
    .Operand2(reservationstation_4_operand2), .InstOp(reservationstation_4_instop),
    .ImmOrAddr(reservationstation_4_immoraddr), .StationId(reservationstation_4_stationid),
    .Ready(reservationstation_4_ready), .Empty(reservationstation_4_empty));
  ReservationStation reservationstation_5 (
    .IdIn(reservationstation_4_stationid), .Instruction(demultiplexer_2_out0), .CDBIn(CDBIn), .clk(Clk),
    .StationSelect(demultiplexer_4_out4), .Clear(or_6_out), .Operand1(reservationstation_5_operand1),
    .Operand2(reservationstation_5_operand2), .InstOp(reservationstation_5_instop),
    .StationId(reservationstation_5_stationid), .Ready(reservationstation_5_ready),
    .Empty(reservationstation_5_empty));  // open: ImmOrAddr
  ReservationStation reservationstation_6 (
    .IdIn(reservationstation_5_stationid), .Instruction(demultiplexer_2_out0), .CDBIn(CDBIn), .clk(Clk),
    .StationSelect(demultiplexer_4_out5), .Clear(or_7_out), .Operand1(reservationstation_6_operand1),
    .Operand2(reservationstation_6_operand2), .InstOp(reservationstation_6_instop),
    .ImmOrAddr(reservationstation_6_immoraddr), .StationId(reservationstation_6_stationid),
    .Ready(reservationstation_6_ready), .Empty(reservationstation_6_empty));
  ReservationStation reservationstation_7 (
    .IdIn(reservationstation_6_stationid), .Instruction(demultiplexer_2_out0), .CDBIn(CDBIn), .clk(Clk),
    .StationSelect(demultiplexer_4_out6), .Clear(or_8_out), .Operand1(reservationstation_7_operand1),
    .Operand2(reservationstation_7_operand2), .InstOp(reservationstation_7_instop),
    .ImmOrAddr(reservationstation_7_immoraddr), .StationId(reservationstation_7_stationid),
    .Ready(reservationstation_7_ready), .Empty(reservationstation_7_empty));
  ReservationStation reservationstation_8 (
    .IdIn(reservationstation_7_stationid), .Instruction(demultiplexer_2_out0), .CDBIn(CDBIn), .clk(Clk),
    .StationSelect(demultiplexer_4_out7), .Clear(or_9_out), .Operand1(reservationstation_8_operand1),
    .Operand2(reservationstation_8_operand2), .InstOp(reservationstation_8_instop),
    .ImmOrAddr(reservationstation_8_immoraddr), .StationId(reservationstation_8_stationid),
    .Ready(reservationstation_8_ready), .Empty(reservationstation_8_empty));
  ReservationStation reservationstation_9 (
    .IdIn(reservationstation_8_stationid), .Instruction(demultiplexer_2_out1), .CDBIn(CDBIn), .clk(Clk),
    .StationSelect(demultiplexer_5_out0), .Clear(demultiplexer_6_out8),
    .Operand1(reservationstation_9_operand1), .Operand2(reservationstation_9_operand2),
    .InstOp(reservationstation_9_instop), .ImmOrAddr(reservationstation_9_immoraddr),
    .StationId(reservationstation_9_stationid), .Ready(reservationstation_9_ready),
    .Empty(reservationstation_9_empty));
  ReservationStation reservationstation_10 (
    .IdIn(reservationstation_9_stationid), .Instruction(demultiplexer_2_out1), .CDBIn(CDBIn), .clk(Clk),
    .StationSelect(demultiplexer_5_out1), .Clear(demultiplexer_6_out9),
    .Operand1(reservationstation_10_operand1), .Operand2(reservationstation_10_operand2),
    .InstOp(reservationstation_10_instop), .ImmOrAddr(reservationstation_10_immoraddr),
    .StationId(reservationstation_10_stationid), .Ready(reservationstation_10_ready),
    .Empty(reservationstation_10_empty));
  ReservationStation reservationstation_11 (
    .IdIn(reservationstation_10_stationid), .Instruction(demultiplexer_2_out1), .CDBIn(CDBIn), .clk(Clk),
    .StationSelect(demultiplexer_5_out2), .Clear(demultiplexer_6_out10),
    .Operand1(reservationstation_11_operand1), .Operand2(reservationstation_11_operand2),
    .InstOp(reservationstation_11_instop), .ImmOrAddr(reservationstation_11_immoraddr),
    .StationId(reservationstation_11_stationid), .Ready(reservationstation_11_ready),
    .Empty(reservationstation_11_empty));
  and and_2 (and_2_out, Clk, commit2);
  Pull_Resistor pull_resistor_6 (.node(pull_resistor_6_node));
  Priority_Encoder #(.select(2)) priority_encoder_1 (
    .in0(reservationstation_1_ready), .in1(reservationstation_2_ready), .in2(reservationstation_3_ready),
    .in3(reservationstation_4_ready), .out(priority_encoder_1_out), .gs(priority_encoder_1_gs));  // open: en_out, en_in
  // Priority_Encoder priority_encoder_2: pin names not known; wires that end beside it: IntFull, reservationstation_1_empty, reservationstation_2_empty, reservationstation_3_empty, reservationstation_4_empty, pull_resistor_6_node, reservationstation_5_empty, reservationstation_6_empty, reservationstation_7_empty, reservationstation_8_empty
  Priority_Encoder #(.select(2)) priority_encoder_3 (
    .in0(reservationstation_9_ready), .in1(reservationstation_10_ready), .in2(reservationstation_11_ready),
    .out(priority_encoder_3_out), .gs(priority_encoder_3_gs));  // open: in3, en_out, en_in
  // Priority_Encoder priority_encoder_4: pin names not known; wires that end beside it: LoadStoreFull, reservationstation_9_empty, reservationstation_10_empty, reservationstation_11_empty, priority_encoder_4_p5
  Priority_Encoder #(.select(2)) priority_encoder_5 (
    .in0(reservationstation_5_ready), .in1(reservationstation_6_ready), .in2(reservationstation_7_ready),
    .in3(reservationstation_8_ready), .out(priority_encoder_5_out), .gs(priority_encoder_5_gs));  // open: en_out, en_in
  Register #(.width(2)) register_1 (.D(priority_encoder_3_out), .en(1'b1), .clk(Clk), .Q(register_1_q), .clr(Clear));
  Register #(.width(1)) register_2 (.D(priority_encoder_3_gs), .en(1'b1), .clk(Clk), .Q(register_2_q), .clr(Clear));
  Register #(.width(2)) register_3 (
    .D(priority_encoder_1_out), .en(1'b1), .clk(and_1_out), .Q(register_3_q), .clr(Clear));
  Register #(.width(1)) register_4 (
    .D(priority_encoder_1_gs), .en(1'b1), .clk(and_1_out), .Q(register_4_q), .clr(Clear));
  Register #(.width(2)) register_5 (
    .D(priority_encoder_5_out), .en(1'b1), .clk(and_2_out), .Q(register_5_q), .clr(Clear));
  Register #(.width(1)) register_6 (
    .D(priority_encoder_5_gs), .en(1'b1), .clk(and_2_out), .Q(register_6_q), .clr(Clear));
  Multiplexer #(.select(2), .width(16), .enable("false")) multiplexer_1 (
    .in0(reservationstation_9_operand1), .in1(reservationstation_10_operand1),
    .in2(reservationstation_11_operand1), .in3(undriven), .out(multiplexer_1_out), .sel(register_1_q));
  Multiplexer #(.select(2), .width(16)) multiplexer_2 (
    .in0(reservationstation_9_operand2), .in1(reservationstation_10_operand2),
    .in2(reservationstation_11_operand2), .out(multiplexer_2_out), .sel(register_1_q), .en(register_2_q));  // open: in3
  Multiplexer #(.select(2), .width(16)) multiplexer_3 (
    .in0(reservationstation_9_immoraddr), .in1(reservationstation_10_immoraddr),
    .in2(reservationstation_11_immoraddr), .out(multiplexer_3_out), .sel(register_1_q), .en(register_2_q));  // open: in3
  Multiplexer #(.select(2), .width(8)) multiplexer_4 (
    .in0(reservationstation_9_instop), .in1(reservationstation_10_instop),
    .in2(reservationstation_11_instop), .out(multiplexer_4_out), .sel(register_1_q), .en(register_2_q));  // open: in3
  Multiplexer #(.select(2), .width(4)) multiplexer_5 (
    .in0(reservationstation_9_stationid), .in1(reservationstation_10_stationid),
    .in2(reservationstation_11_stationid), .out(multiplexer_5_out), .sel(register_1_q), .en(register_2_q));  // open: in3
  Multiplexer #(.select(2), .width(16)) multiplexer_6 (
    .in0(reservationstation_1_operand1), .in1(reservationstation_2_operand1),
    .in2(reservationstation_3_operand1), .in3(reservationstation_4_operand1), .out(multiplexer_6_out),
    .sel(register_3_q), .en(register_4_q));
  Multiplexer #(.select(2), .width(16)) multiplexer_7 (
    .in0(reservationstation_1_operand2), .in1(reservationstation_2_operand2),
    .in2(reservationstation_3_operand2), .in3(reservationstation_4_operand2), .out(multiplexer_7_out),
    .sel(register_3_q), .en(register_4_q));
  Multiplexer #(.select(2), .width(8)) multiplexer_8 (
    .in0(reservationstation_1_instop), .in1(reservationstation_2_instop), .in2(reservationstation_3_instop),
    .in3(reservationstation_4_instop), .out(multiplexer_8_out), .sel(register_3_q), .en(register_4_q));
  Multiplexer #(.select(2), .width(4)) multiplexer_9 (
    .in0(reservationstation_1_stationid), .in1(reservationstation_2_stationid),
    .in2(reservationstation_3_stationid), .in3(reservationstation_4_stationid), .out(pull_resistor_4_node),
    .sel(register_3_q), .en(register_4_q));
  Multiplexer #(.select(2), .width(16)) multiplexer_10 (
    .in0(reservationstation_1_immoraddr), .in1(reservationstation_2_immoraddr),
    .in2(reservationstation_3_immoraddr), .in3(reservationstation_4_immoraddr), .out(multiplexer_10_out),
    .sel(register_3_q), .en(register_4_q));
  Multiplexer #(.select(2), .width(16)) multiplexer_11 (
    .in0(reservationstation_5_operand1), .in1(reservationstation_6_operand1),
    .in2(reservationstation_7_operand1), .in3(reservationstation_8_operand1), .out(multiplexer_11_out),
    .sel(register_5_q), .en(register_6_q));
  Pull_Resistor pull_resistor_7 (.node(multiplexer_11_out));
  Pull_Resistor pull_resistor_8 (.node(pull_resistor_8_node));
  Multiplexer #(.select(2), .width(16)) multiplexer_12 (
    .in0(reservationstation_5_operand2), .in1(reservationstation_6_operand2),
    .in2(reservationstation_7_operand2), .in3(reservationstation_8_operand2), .out(pull_resistor_8_node),
    .sel(register_5_q), .en(register_6_q));
  Multiplexer #(.select(2), .width(8)) multiplexer_13 (
    .in0(reservationstation_5_instop), .in1(reservationstation_6_instop), .in2(reservationstation_7_instop),
    .in3(reservationstation_8_instop), .out(multiplexer_13_out), .sel(register_5_q), .en(register_6_q));
  Pull_Resistor pull_resistor_9 (.node(multiplexer_13_out));
  Pull_Resistor pull_resistor_10 (.node(pull_resistor_1_node));
  Multiplexer #(.select(2), .width(4)) multiplexer_14 (
    .in0(reservationstation_5_stationid), .in1(reservationstation_6_stationid),
    .in2(reservationstation_7_stationid), .in3(reservationstation_8_stationid), .out(pull_resistor_1_node),
    .sel(register_5_q), .en(register_6_q));
  Pull_Resistor pull_resistor_11 (.node(pull_resistor_11_node));
  Multiplexer #(.select(2), .width(16)) multiplexer_15 (
    .in0(reservationstation_6_immoraddr), .in1(reservationstation_7_immoraddr),
    .in2(reservationstation_8_immoraddr), .out(pull_resistor_11_node), .sel(register_5_q), .en(register_6_q));  // open: in3
  Pull_Resistor pull_resistor_12 (.node(multiplexer_6_out));
  Pull_Resistor pull_resistor_13 (.node(multiplexer_7_out));
  Pull_Resistor pull_resistor_14 (.node(multiplexer_8_out));
  Pull_Resistor pull_resistor_15 (.node(pull_resistor_4_node));
  Pull_Resistor pull_resistor_16 (.node(multiplexer_10_out));
  FunctionalUnit functionalunit_1 (
    .Operand1(multiplexer_11_out), .Operand2(pull_resistor_8_node), .Op(multiplexer_13_out),
    .Run(register_6_q), .Immediate(pull_resistor_11_node), .Result(functionalunit_1_result), .Done(commit2));
  FunctionalUnit functionalunit_2 (
    .Operand1(multiplexer_6_out), .Operand2(multiplexer_7_out), .Op(multiplexer_8_out), .Run(register_4_q),
    .Immediate(multiplexer_10_out), .Result(functionalunit_2_result), .Done(commit1));
  LoadStoreTranslator loadstoretranslator_1 (
    .Operand1(multiplexer_1_out), .Operand2(multiplexer_2_out), .Imm(multiplexer_3_out),
    .Op(multiplexer_4_out), .Run(register_2_q), .VAddr(VAddress), .Data(Data), .Load(Load), .Store(Store),
    .Done(loadstoretranslator_1_done));
  ToCDB tocdb_1 (.SourceStation(pull_resistor_1_node), .Data(functionalunit_1_result), .CDBOut(CDB2));
  ToCDB tocdb_2 (.SourceStation(pull_resistor_4_node), .Data(functionalunit_2_result), .CDBOut(CDB1));
endmodule

module FunctionalUnit (
  input  [15:0] Operand1,
  input  [15:0] Operand2,
  input  [7:0] Op,
  input  Run,
  input  [15:0] Immediate,
  output [15:0] Result,
  output Done
);

  wire [3:0] bit_extender_1_out, bit_extender_2_out, bit_extender_3_out;
  wire [7:0] controlled_buffer_1_out;
  wire [15:0] adder_1_out, divider_1_out, multiplier_1_out, shifter_1_out, shifter_2_out, shifter_3_out,
       subtractor_1_out;

  assign controlled_buffer_1_out = Run ? Op : 8'bz;  // Controlled_Buffer controlled_buffer_1
  Adder #(.width(16)) adder_1 (.b(Operand2), .out(adder_1_out));  // open: a, cin, cout
  Subtractor #(.width(16)) subtractor_1 (.a(Operand1), .b(Operand2), .out(subtractor_1_out));  // open: bin, bout
  Multiplier #(.width(16)) multiplier_1 (.a(Operand1), .b(Operand2), .out(multiplier_1_out));  // open: cin, cout
  Divider #(.width(16)) divider_1 (.a(Operand1), .b(Operand2), .out(divider_1_out));  // open: upper, rem
  Shifter #(.width(16)) shifter_1 (.in(Operand1), .\dist (bit_extender_1_out), .out(shifter_1_out));
  Bit_Extender #(.in_width(16), .out_width(4), .\type ("zero")) bit_extender_1 (
    .in(Operand2), .out(bit_extender_1_out));
  Shifter #(.width(16), .shift("lr")) shifter_2 (.in(Operand1), .\dist (bit_extender_2_out), .out(shifter_2_out));
  Bit_Extender #(.in_width(16), .out_width(4), .\type ("zero")) bit_extender_2 (
    .in(Operand2), .out(bit_extender_2_out));
  Shifter #(.width(16), .shift("ar")) shifter_3 (.in(Operand1), .\dist (bit_extender_3_out), .out(shifter_3_out));
  Bit_Extender #(.in_width(16), .out_width(4), .\type ("zero")) bit_extender_3 (
    .in(Operand2), .out(bit_extender_3_out));
  Multiplexer #(.select(3), .width(16), .enable("false")) multiplexer_1 (
    .in0(Operand1), .in1(adder_1_out), .in2(subtractor_1_out), .in3(multiplier_1_out), .in4(divider_1_out),
    .in5(shifter_1_out), .in6(shifter_2_out), .in7(shifter_3_out), .out(Result));  // open: sel
  Pull_Resistor pull_resistor_1 (.node(Done));
  buf buffer_1 (Done, Run);
endmodule

module ReservationStation (
  input  [3:0] IdIn,
  input  [31:0] Instruction,
  input  [31:0] CDBIn,
  input  clk,
  input  StationSelect,
  input  Clear,
  output [15:0] Operand1,
  output [15:0] Operand2,
  output [7:0] InstOp,
  output [15:0] ImmOrAddr,
  output [3:0] StationId,
  output Ready,
  output Empty
);

  wire and_1_out, comparator_1_eq, comparator_1_gt, comparator_2_eq, comparator_3_eq, comparator_4_gt,
       comparator_5_gt, comparator_6_eq, comparator_7_eq, comparator_8_eq, controlled_buffer_2_out,
       not_1_out, not_2_out, not_3_out, not_4_out, or_1_out, or_2_out, pull_resistor_2_node;
  wire [3:0] register_2_q, register_5_q;
  wire [31:0] controlled_buffer_1_out;

  assign controlled_buffer_1_out = StationSelect ? Instruction : 32'bz;  // Controlled_Buffer controlled_buffer_1
  Pull_Resistor pull_resistor_1 (.node(controlled_buffer_1_out));
  Register register_1 (.D(controlled_buffer_1_out[31:24]), .en(StationSelect), .clk(clk), .Q(InstOp), .clr(Clear));
  Comparator #(.width(4), .mode("unsigned")) comparator_1 (
    .a(CDBIn[19:16]), .b(4'b0000), .gt(comparator_1_gt), .eq(comparator_1_eq));  // open: lt
  Comparator #(.width(4), .mode("unsigned")) comparator_2 (
    .a(register_2_q), .b(CDBIn[19:16]), .eq(comparator_2_eq));  // open: gt, lt
  Comparator #(.width(4), .mode("unsigned")) comparator_3 (
    .a(register_5_q), .b(CDBIn[19:16]), .eq(comparator_3_eq));  // open: gt, lt
  and and_1 (and_1_out, comparator_1_gt, clk);
  not not_1 (not_1_out, comparator_1_eq);
  assign controlled_buffer_2_out = not_1_out ? comparator_3_eq : 1'bz;  // Controlled_Buffer controlled_buffer_2
  Register #(.width(4)) register_2 (
    .D(controlled_buffer_1_out[19:16]), .en(StationSelect), .clk(clk), .Q(register_2_q), .clr(or_1_out));
  or or_1 (or_1_out, comparator_4_gt, Clear);
  Pull_Resistor pull_resistor_2 (.node(pull_resistor_2_node));
  assign pull_resistor_2_node = not_1_out ? comparator_2_eq : 1'bz;  // Controlled_Buffer controlled_buffer_3
  Pull_Resistor pull_resistor_3 (.node(controlled_buffer_2_out));
  Register #(.width(16)) register_3 (
    .D(CDBIn[15:0]), .en(pull_resistor_2_node), .clk(and_1_out), .Q(Operand1), .clr(Clear));
  Register #(.width(16)) register_4 (
    .D(controlled_buffer_1_out[31:16]), .en(StationSelect), .clk(clk), .Q(ImmOrAddr), .clr(Clear));
  Comparator #(.width(16), .mode("unsigned")) comparator_4 (
    .a(Operand1), .b({16{1'b0}}), .gt(comparator_4_gt));  // open: eq, lt
  Register #(.width(4)) register_5 (
    .D(controlled_buffer_1_out[15:12]), .en(StationSelect), .clk(clk), .Q(register_5_q), .clr(or_2_out));
  or or_2 (or_2_out, comparator_5_gt, Clear);
  Register #(.width(16)) register_6 (
    .D(CDBIn[15:0]), .en(controlled_buffer_2_out), .clk(and_1_out), .Q(Operand2), .clr(Clear));
  Comparator #(.width(16), .mode("unsigned")) comparator_5 (
    .a(Operand2), .b({16{1'b0}}), .gt(comparator_5_gt));  // open: eq, lt
  Pull_Resistor pull_resistor_4 (.node(Operand1));
  Pull_Resistor pull_resistor_5 (.node(Operand2));
  Pull_Resistor pull_resistor_6 (.node(InstOp));
  Pull_Resistor pull_resistor_7 (.node(ImmOrAddr));
  Adder #(.width(4)) adder_1 (.a(IdIn), .b(4'b0001), .out(StationId));  // open: cin, cout
  Comparator #(.width(4), .mode("unsigned")) comparator_6 (
    .a(register_5_q), .b(4'b0000), .eq(comparator_6_eq));  // open: gt, lt
  Comparator #(.width(4), .mode("unsigned")) comparator_7 (
    .a(register_2_q), .b(4'b0000), .eq(comparator_7_eq));  // open: gt, lt
  Comparator #(.mode("unsigned")) comparator_8 (.a(InstOp), .b({8{1'b0}}), .eq(comparator_8_eq));  // open: gt, lt
  not not_2 (not_2_out, comparator_8_eq);
  and and_2 (Ready, comparator_6_eq, comparator_7_eq, not_2_out);
  not not_3 (not_3_out, comparator_6_eq);
  not not_4 (not_4_out, comparator_7_eq);
  nor nor_1 (Empty, not_3_out, not_4_out, not_2_out);
  Pull_Resistor pull_resistor_8 (.node(Ready));
  Pull_Resistor pull_resistor_9 (.node(Empty));

  // Notes on the sheet:
  //   ImmOrAddr: pull=down
  //   Operand2: pull=down
endmodule

module ToCDB (
  input  [3:0] SourceStation,
  input  [15:0] Data,
  output [31:0] CDBOut
);

  Pull_Resistor pull_resistor_1 (.node({CDBOut[31:20], SourceStation, Data}));

  assign CDBOut[19:0] = {SourceStation, Data};
endmodule

module LoadStoreTranslator (
  input  [15:0] Operand1,
  input  [15:0] Operand2,
  input  [15:0] Imm,
  input  [7:0] Op,
  input  Run,
  output [23:0] VAddr,
  output [15:0] Data,
  output Load,
  output Store,
  output Done
);

  wire [7:0] controlled_buffer_1_out;

  Bit_Extender #(.in_width(16), .out_width(8), .\type ("zero")) bit_extender_1 (.in(Operand1), .out(VAddr[23:16]));
  assign controlled_buffer_1_out = Run ? Op : 8'bz;  // Controlled_Buffer controlled_buffer_1
  Comparator comparator_1 (.a(controlled_buffer_1_out), .b(8'h20), .eq(Load));  // open: gt, lt
  Comparator comparator_2 (.a(controlled_buffer_1_out), .b(8'h21), .eq(Store));  // open: gt, lt
  Pull_Resistor pull_resistor_1 (.node({VAddr[23:16], Operand2}));
  Pull_Resistor pull_resistor_2 (.node(Imm));
  Pull_Resistor pull_resistor_3 (.node(Load));
  Pull_Resistor pull_resistor_4 (.node(Store));
  Pull_Resistor pull_resistor_5 (.node(Done));
  buf buffer_1 (Done, Run);

  assign Data = Imm;
  assign VAddr[15:0] = Operand2;
endmodule

module LoadStoreUnit (
  input  [23:0] Address,
  input  [15:0] Value,
  input  Store,
  input  [15:0] ValueFromRam,
  input  Load,
  input  Clk,
  output [23:0] RamAddress,
  output [15:0] RamValue
);
endmodule

module FromCDB (
  input  [31:0] CDBIn,
  output [3:0] SourceStation,
  output [15:0] Data
);


  assign Data = CDBIn[15:0];
  assign SourceStation = CDBIn[19:16];
endmodule

module InstructionBuffer (
  input  ClearBuffer,
  input  BufferClk,
  input  NextInstruction,
  input  [31:0] Instruction,
  output LoadNext,
  output [31:0] NextInst
);

  wire and_1_out, not_1_out, or_1_out;
  wire [31:0] shift_register_1_p6;

  and and_1 (and_1_out, BufferClk, LoadNext);
  not not_1 (not_1_out, LoadNext);
  Pull_Resistor pull_resistor_1 (.node(not_1_out));
  or or_1 (or_1_out, and_1_out, NextInstruction);
  // Shift_Register #(.width(32), .length(16)) shift_register_1: pin names not known; wires that end beside it: ClearBuffer, and_1_out, not_1_out, or_1_out, Instruction, shift_register_1_p6
  Comparator #(.width(32)) comparator_1 (.a({32{1'b0}}), .b(shift_register_1_p6), .eq(LoadNext));  // open: gt, lt
endmodule
